# Fritzing sketch ProjetSmartPatate (saved by Fritzing 0.9.3b)
breadboards: 1

parts:
  Composant1 = Arduino Uno (Rev3)
  L1 = Inductor [package="400 mil [THT]"]
  R1 = Resistor [tolerance=±5% resistance=220 package="0603 [SMD]"]
  C1 = Capacitor [package=cap-pth-small-kit]
  R2 = Resistor [tolerance=±5% resistance=220 package="0603 [SMD]"]
  R3 = 220 Ω Resistor [package="0603 [SMD]"]
  D1 = Rectifier Diode [part_number=1N4001 package="300 mil [THT]"]
  C2 = Ceramic Capacitor [capacitance=100nF package="100 mil [THT, multilayer]"]
  LED1 = smd LED [color="Red (633nm)" package="1206 [SMD]"]
  LED2 = smd LED [color="Red (633nm)" package="1206 [SMD]"]

nets:
  N1: Composant1.A0, R3.Pin_1, D1.cathode, C2.1
  N2: Composant1.D9_PWM, R1.Pin_0
  N3: Composant1.D3_PWM, Composant1.D7, Composant1.GND, R2.Pin_0, R3.ResVert, C2.0
  N4: L1.pin_0, R1.Pin_1, R2.Pin_1
  N5: L1.pin_1, C1.1
  N6: C1.2, D1.anode
  N7: LED1.cathode, LED2.cathode

custom parts:
  Arduino Uno (Rev3): The Arduino Uno is a microcontroller board based on the ATmega328 (datasheet). It has 14 digital input/output pins (of which 6 can be used as PWM outputs), 6 analog inputs, a 16 MHz ceramic resonator, a USB connection, a power jack, an ICSP header, and a reset button. It contains everything needed to support the microcontroller; simply connect it to a computer with a USB cable or power it with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
  220 Ω Resistor: A generic resistor (0.25W)
